# Fritzing sketch design (saved by Fritzing 0.9.10b)

parts:
  Mod1 = Amica NodeMCU DEVKIT 1.0
  E1 = LoRa E32-TTL-100 EBYTE 433MHz [package="SIP (Single Inline) [THT]"]
  R1_(stability) = Resistor [tolerance=±5% resistance=4.7k package="1206 [SMD]"]
  R2_(stability) = Resistor [tolerance=±5% resistance=4.7k package="1206 [SMD]"]

nets:
  N1: Mod1.pin6, E1.M0
  N2: Mod1.pin7, E1.M1
  N3: Mod1.pin8, E1.AUX
  N4: Mod1.pin_9, Mod1.pin_25, E1.GND
  N5: Mod1.pin_10, Mod1.pin_26, E1.VCC, R1_(stability).Pin_1, R2_(stability).Pin_1
  N6: Mod1.pin_11, E1.RX, R2_(stability).Pin_0
  N7: Mod1.pin_12, E1.TX, R1_(stability).Pin_0

custom parts:
  LoRa E32-TTL-100 EBYTE 433MHz: A SIP stand-in part for whatever you want. With 7 pins on a 300 mil single inline package (SIP) footprint.
