# Fritzing sketch design (saved by Fritzing 0.9.10b)

parts:
  Mod1 = Amica NodeMCU DEVKIT 1.0
  Part2 = INA219 High Side DC Current Sensor Breakout [part_number=904]
  Part3 = OLED Monochrome 128x32 I2C [part_number=931]
  Part4 = MPL3115A2 I2C Barometric Pressure, Altitude, Temperature Sensor
  CONN1 = USB connector [package=THT]
  E1 = LoRa E32-TTL-100 EBYTE 433MHz [package="SIP (Single Inline) [THT]"]
  R1_(stability) = Resistor [tolerance=±5% resistance=4.7k package="1206 [SMD]"]
  R2_(stability) = Resistor [tolerance=±5% resistance=4.7k package="1206 [SMD]"]

nets:
  N1: Mod1.pin6, E1.M0
  N2: Mod1.pin7, E1.M1
  N3: Mod1.pin8, E1.AUX
  GND: Mod1.pin_9, Mod1.pin_25, Part2.GND, Part3.GND, Part4.GND, E1.GND
  VCC: Mod1.pin_10, Mod1.pin_26, Part2.VCC, Part3.3.3V, Part4.VIN, E1.VCC, R1_(stability).Pin_1, R2_(stability).Pin_1
  N4: Mod1.pin_11, E1.RX, R2_(stability).Pin_0
  N5: Mod1.pin_12, E1.TX, R1_(stability).Pin_0
  N6: Mod1.pin_13, Part2.SDA, Part3.SDA, Part4.SDA
  N7: Mod1.pin_14, Part2.SCL, Part3.SCL, Part4.SCL
  N8: Part2.VIN-, CONN1.GND, CONN1.chassis5, CONN1.chassis6

custom parts:
  INA219 High Side DC Current Sensor Breakout: This breakout board will solve all your power-monitoring problems. Instead of struggling with two multimeters, you can just use the handy INA219B chip on this breakout to both measure both the high side voltage and DC current draw over I2C with 1% precision. Most current-measuring devices such as our current panel meter are only good for low side measuring. That means that unless you want to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
  OLED Monochrome 128x32 I2C: These displays are small, only about 1" diagonal, but very readable due to the high contrast of an OLED display. This display is made of 128x32 individual white OLED pixels, each one is turned on or off by the controller chip. Because the display makes its own light, no backlight is required. This reduces the power required to run the OLED and is why the display has such high contrast; we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
  MPL3115A2 I2C Barometric Pressure, Altitude, Temperature Sensor: This pressure sensor from Freescale is a great low-cost sensing solution for precision measurement of barometric pressure and altitude. The MPL3115A2 has a typical 1.5 Pascal resolution, which can resolve altitude at 0.3 meters (compare to the BMP180 which can do 0.17m). It has some upsides compared to the BMP180, such as interrupt outputs for ultra-low power usage, and its also a heck of a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
  LoRa E32-TTL-100 EBYTE 433MHz: A SIP stand-in part for whatever you want. With 7 pins on a 300 mil single inline package (SIP) footprint.
